// Logisim project Relatorio02.circ as structural Verilog: 6 circuits, main circuit main
module main (
  input  [3:0] A,
  input  [3:0] B,
  input  Cin,
  output Cout,
  output [3:0] S
);

  wire completosomador_2_cout, completosomador_3_cout, completosomador_4_cout, multiplexer_1_out,
       multiplexer_2_out, multiplexer_3_out, multiplexer_4_out, not_1_out, not_2_out, not_3_out, not_4_out;

  not not_1 (not_1_out, B[3]);
  Multiplexer #(.enable("false")) multiplexer_1 (.in0(B[3]), .in1(not_1_out), .out(multiplexer_1_out), .sel(Cin));
  completoSomador completosomador_1 (
    .S(S[3]), .A(A[3]), .Cout(Cout), .Cin(completosomador_2_cout), .B(multiplexer_1_out));
  not not_2 (not_2_out, B[2]);
  Multiplexer #(.enable("false")) multiplexer_2 (.in0(B[2]), .in1(not_2_out), .out(multiplexer_2_out), .sel(Cin));
  completoSomador completosomador_2 (
    .S(S[2]), .A(A[2]), .Cout(completosomador_2_cout), .Cin(completosomador_3_cout), .B(multiplexer_2_out));
  not not_3 (not_3_out, B[1]);
  Multiplexer #(.enable("false")) multiplexer_3 (.in0(B[1]), .in1(not_3_out), .out(multiplexer_3_out), .sel(Cin));
  completoSomador completosomador_3 (
    .S(S[1]), .A(A[1]), .Cout(completosomador_3_cout), .Cin(completosomador_4_cout), .B(multiplexer_3_out));
  not not_4 (not_4_out, B[0]);
  Multiplexer #(.enable("false")) multiplexer_4 (.in0(B[0]), .in1(not_4_out), .out(multiplexer_4_out), .sel(Cin));
  completoSomador completosomador_4 (
    .S(S[0]), .A(A[0]), .Cout(completosomador_4_cout), .Cin(Cin), .B(multiplexer_4_out));
endmodule

module meioSomador (
  input  A,
  input  B,
  output S,
  output Cout
);

  xor xor_1 (S, A, B);
  and and_1 (Cout, B, A);
endmodule

module completoSomador (
  input  A,
  input  B,
  input  Cin,
  output S,
  output Cout
);

  wire meiosomador_1_cout, meiosomador_1_s, meiosomador_2_cout;

  meioSomador meiosomador_1 (.Cout(meiosomador_1_cout), .S(meiosomador_1_s), .A(A), .B(B));
  meioSomador meiosomador_2 (.Cout(meiosomador_2_cout), .S(S), .A(meiosomador_1_s), .B(Cin));
  or or_1 (Cout, meiosomador_2_cout, meiosomador_1_cout);
endmodule

module complementoDois (
  input  [3:0] A,
  input  [3:0] B,
  input  Cin,
  output Cout,
  output [3:0] S
);

  wire completosomador_2_cout, completosomador_3_cout, completosomador_4_cout, multiplexer_1_out,
       multiplexer_2_out, multiplexer_3_out, multiplexer_4_out, not_1_out, not_2_out, not_3_out, not_4_out;

  not not_1 (not_1_out, B[3]);
  Multiplexer #(.enable("false")) multiplexer_1 (.in0(B[3]), .in1(not_1_out), .out(multiplexer_1_out), .sel(Cin));
  completoSomador completosomador_1 (
    .S(S[3]), .A(A[3]), .Cout(Cout), .Cin(completosomador_2_cout), .B(multiplexer_1_out));
  not not_2 (not_2_out, B[2]);
  Multiplexer #(.enable("false")) multiplexer_2 (.in0(B[2]), .in1(not_2_out), .out(multiplexer_2_out), .sel(Cin));
  completoSomador completosomador_2 (
    .S(S[2]), .A(A[2]), .Cout(completosomador_2_cout), .Cin(completosomador_3_cout), .B(multiplexer_2_out));
  not not_3 (not_3_out, B[1]);
  Multiplexer #(.enable("false")) multiplexer_3 (.in0(B[1]), .in1(not_3_out), .out(multiplexer_3_out), .sel(Cin));
  completoSomador completosomador_3 (
    .S(S[1]), .A(A[1]), .Cout(completosomador_3_cout), .Cin(completosomador_4_cout), .B(multiplexer_3_out));
  not not_4 (not_4_out, B[0]);
  Multiplexer #(.enable("false")) multiplexer_4 (.in0(B[0]), .in1(not_4_out), .out(multiplexer_4_out), .sel(Cin));
  completoSomador completosomador_4 (
    .S(S[0]), .A(A[0]), .Cout(completosomador_4_cout), .Cin(Cin), .B(multiplexer_4_out));
endmodule

module multiplicacao (
  input  A0,
  input  A1,
  input  B1,
  input  B0,
  output P3,
  output P2,
  output P1,
  output P0
);

  wire and_1_out, and_2_out, and_3_out, meiosomador_2_cout;

  and and_1 (and_1_out, A1, B1);
  meioSomador meiosomador_1 (.Cout(P3), .S(P2), .A(meiosomador_2_cout), .B(and_1_out));
  and and_2 (and_2_out, A1, B0);
  and and_3 (and_3_out, A0, B1);
  meioSomador meiosomador_2 (.Cout(meiosomador_2_cout), .S(P1), .A(and_3_out), .B(and_2_out));
  and and_4 (P0, A0, B0);
endmodule

module registradorDeslocamento (
  input  [3:0] D,
  input  Clock,
  input  Carga,
  input  Clear,
  output [3:0] Q
);

  wire multiplexer_1_out, multiplexer_2_out, multiplexer_3_out, multiplexer_4_out;

  D_Flip_Flop d_ff_1 (.D(multiplexer_1_out), .clk(Clock), .Q(Q[3]), .reset(Clear));  // open: Qn, preset
  Multiplexer #(.enable("false")) multiplexer_1 (.in0(Q[3]), .in1(D[3]), .out(multiplexer_1_out), .sel(Carga));
  Multiplexer #(.enable("false")) multiplexer_2 (.in0(Q[2]), .in1(D[2]), .out(multiplexer_2_out), .sel(Carga));
  D_Flip_Flop d_ff_2 (.D(multiplexer_2_out), .clk(Clock), .Q(Q[2]), .reset(Clear));  // open: Qn, preset
  D_Flip_Flop d_ff_3 (.D(multiplexer_3_out), .clk(Clock), .Q(Q[1]), .reset(Clear));  // open: Qn, preset
  Multiplexer #(.enable("false")) multiplexer_3 (.in0(Q[1]), .in1(D[1]), .out(multiplexer_3_out), .sel(Carga));
  Multiplexer #(.enable("false")) multiplexer_4 (.in1(D[0]), .out(multiplexer_4_out), .sel(Carga));  // open: in0
  D_Flip_Flop d_ff_4 (.D(multiplexer_4_out), .clk(Clock), .Q(Q[0]), .reset(Clear));  // open: Qn, preset
endmodule
