// Logisim project Relatorio01.circ as structural Verilog: 6 circuits, main circuit main
module main (
  input  [1:0] in_1,
  input  Escolha,
  input  [2:0] in_3,
  input  Escolha2,
  output [1:0] out_5,
  output [1:0] out_6
);

  wire [1:0] completosomador_1_s, completosubtrator_1_s, demultiplexer_1_out0, demultiplexer_1_out1,
       meiosomador_1_s, meiosubtrator_1_s;
  wire [2:0] demultiplexer_2_out0, demultiplexer_2_out1;

  Demultiplexer #(.width(2), .enable("false")) demultiplexer_1 (
    .out0(demultiplexer_1_out0), .out1(demultiplexer_1_out1), .in(in_1), .sel(Escolha));
  Demultiplexer #(.width(3), .enable("false")) demultiplexer_2 (
    .out0(demultiplexer_2_out0), .out1(demultiplexer_2_out1), .in(in_3), .sel(Escolha2));
  meioSubtrator meiosubtrator_1 (
    .Tout(meiosubtrator_1_s[1]), .B(demultiplexer_1_out1[1]), .A(demultiplexer_1_out1[0]),
    .S(meiosubtrator_1_s[0]));
  meioSomador meiosomador_1 (
    .Cout(meiosomador_1_s[1]), .B(demultiplexer_1_out0[0]), .A(demultiplexer_1_out0[1]),
    .S(meiosomador_1_s[0]));
  completoSomador completosomador_1 (
    .S(completosomador_1_s[0]), .B(demultiplexer_2_out0[1]), .A(demultiplexer_2_out0[2]),
    .Cin(demultiplexer_2_out0[0]), .Cout(completosomador_1_s[1]));
  completoSubtrator completosubtrator_1 (
    .S(completosubtrator_1_s[0]), .B(demultiplexer_2_out1[1]), .Bin(demultiplexer_2_out1[0]),
    .Bout(completosubtrator_1_s[1]), .A(demultiplexer_2_out1[2]));
  Multiplexer #(.width(2), .enable("false")) multiplexer_1 (
    .in0(meiosomador_1_s), .in1(meiosubtrator_1_s), .out(out_5), .sel(Escolha));
  Multiplexer #(.width(2), .enable("false")) multiplexer_2 (
    .in0(completosomador_1_s), .in1(completosubtrator_1_s), .out(out_6), .sel(Escolha2));
endmodule

module meioSomador (
  input  A,
  input  B,
  output S,
  output Cout
);

  xor xor_1 (S, A, B);
  and and_1 (Cout, B, A);
endmodule

module completoSomador (
  input  A,
  input  B,
  input  Cin,
  output S,
  output Cout
);

  wire meiosomador_1_cout, meiosomador_1_s, meiosomador_2_cout;

  meioSomador meiosomador_1 (.Cout(meiosomador_1_cout), .B(B), .A(A), .S(meiosomador_1_s));
  meioSomador meiosomador_2 (.Cout(meiosomador_2_cout), .B(Cin), .A(meiosomador_1_s), .S(S));
  or or_1 (Cout, meiosomador_2_cout, meiosomador_1_cout);
endmodule

module Somador_4bits (
  input  [3:0] A,
  input  [3:0] B,
  output [3:0] S
);

  wire completosomador_1_cout, completosomador_2_cout, completosomador_3_cout, completosomador_4_cout;

  Hex_Digit_Display hex_digit_display_1 (.value(S));  // open: dp
  completoSomador completosomador_1 (
    .S(S[3]), .B(B[3]), .A(A[3]), .Cin(completosomador_2_cout), .Cout(completosomador_1_cout));
  completoSomador completosomador_2 (
    .S(S[2]), .B(B[2]), .A(A[2]), .Cin(completosomador_3_cout), .Cout(completosomador_2_cout));
  completoSomador completosomador_3 (
    .S(S[1]), .B(B[1]), .A(A[1]), .Cin(completosomador_4_cout), .Cout(completosomador_3_cout));
  completoSomador completosomador_4 (.S(S[0]), .B(B[0]), .A(A[0]), .Cin(1'b0), .Cout(completosomador_4_cout));
  // also tied to GND on the sheet: completosomador_1_cout
endmodule

module meioSubtrator (
  input  A,
  input  B,
  output S,
  output Tout
);

  wire not_1_out;

  xor xor_1 (S, A, B);
  and and_1 (Tout, B, not_1_out);
  not not_1 (not_1_out, A);
endmodule

module completoSubtrator (
  input  A,
  input  B,
  input  Bin,
  output S,
  output Bout
);

  wire meiosubtrator_1_s, meiosubtrator_1_tout, meiosubtrator_2_tout;

  meioSubtrator meiosubtrator_1 (.Tout(meiosubtrator_1_tout), .B(B), .A(A), .S(meiosubtrator_1_s));
  meioSubtrator meiosubtrator_2 (.Tout(meiosubtrator_2_tout), .B(Bin), .A(meiosubtrator_1_s), .S(S));
  or or_1 (Bout, meiosubtrator_2_tout, meiosubtrator_1_tout);
endmodule
